# Fritzing sketch Proyecto (saved by Fritzing 0.9.10b)
breadboards: 1

parts:
  Part1 = Arduino Uno (Rev3)
  PWM1 = PCA9685 16x12-bit PWM Breakout
  J1 = Basic Servo
  J2 = Basic Servo
  J3 = Basic Servo
  J4 = Basic Servo
  Mod1 = Raspberry Pi 4B
  USBTTL1 = Micro USB B Plug
  USBTTL2 = USB A Plug
  CAMERA1 = TTL Serial JPEG Camera

nets:
  N1: Part1.A4/SDA, PWM1.no_name_yet#504
  N2: Part1.A5/SCL, PWM1.no_name_yet#503
  N3: Part1.5V, PWM1.no_name_yet#505
  N4: Part1.GND, PWM1.no_name_yet#501, PWM1.no_name_yet#1000, PWM1.no_name_yet#1001, PWM1.no_name_yet#1002, PWM1.no_name_yet#1003
  N5: PWM1.no_name_yet#0, J1.pulse
  N6: PWM1.no_name_yet#1, J2.pulse
  N7: PWM1.no_name_yet#2, J3.pulse
  N8: PWM1.no_name_yet#3, J4.pulse
  N9: PWM1.no_name_yet#100, PWM1.no_name_yet#101, PWM1.no_name_yet#102, PWM1.no_name_yet#103
  5V: Mod1.5V, CAMERA1.5V
  GND: Mod1.GND, CAMERA1.GND
  N10: Mod1.GPIO14, CAMERA1.RX
  N11: Mod1.GPIO15, CAMERA1.TX
  N12: USBTTL1.usb, USBTTL2.usb

custom parts:
  USB A Plug: USB A Plug breadboard only for documetnation purposes.
  TTL Serial JPEG Camera: TTL Serial JPEG Camera with NTSC Out
