# Fritzing sketch ex (saved by Fritzing 0.9.10b)
breadboards: 1

parts:
  Part2 = Arduino Mega 2560 (Rev3)
  U1 = POT [knob_status=50% power=0.5W package=pot_alpha_rv16af-20]
  U2 = POT [knob_status=50% power=0.5W package=pot_alpha_rv16af-20]
  S1 = Pushbutton [package="[THT]"]
  S2 = Pushbutton [package="[THT]"]
  S3 = Pushbutton [package="[THT]"]
  R1 = Resistor [tolerance=±5% resistance=220 package="0805 [SMD]"]
  R2 = Resistor [tolerance=±5% resistance=220 package="0805 [SMD]"]
  R3 = Resistor [tolerance=±5% resistance=220 package="0805 [SMD]"]

nets:
  N1: Part2.A0, U1.S
  N2: Part2.A1, U2.S
  N3: Part2.5V, U1.A, U2.A, R1.Pin_1, R2.Pin_1, R3.Pin_1
  N4: Part2.GND, U1.E, U2.E, S1.Pin_3, S1.Pin_4, S2.Pin_3, S2.Pin_4, S3.Pin_3, S3.Pin_4
  N5: Part2.D2_PWM, S3.Pin_1, S3.Pin_2, R1.Pin_0
  N6: Part2.D3_PWM, S2.Pin_1, S2.Pin_2, R2.Pin_0
  N7: Part2.D4_PWM, S1.Pin_1, S1.Pin_2, R3.Pin_0
